# Fritzing sketch sketch (saved by Fritzing 0.9.3b)
breadboards: 1

parts:
  Componente1 = Arduino Uno (Rev3)
  J1 = Basic Servo
  J2 = Basic Servo
  J3 = Piezo Speaker
  T1 = LM35 Temperature Sensor [package="TO92 [THT]"]
  PIR1 = PIR sensor

nets:
  N1: Componente1.D8, J3.pin2
  N2: Componente1.D10_PWM/SS, J2.pulse
  N3: Componente1.D11_PWM/MOSI, J1.pulse
  GND: J1.gnd, J2.gnd, J3.pin1, T1.Vout, PIR1.GND
  VCC: J1.vcc, J2.vcc, T1.+Vs, PIR1.VDD
